# Fritzing sketch circruit (saved by Fritzing 1.0.7)

parts:
  U1 = ESP32-38PinWide [part_number=ESP32-38PinWide]
  Part1 = Thumb Joystick
  LCD1 = TFT 1.8 inch 160x128 no SD
  Part2 = Adafruit MAX98357A I2S 3W Class D Amplifier [part_number="Adafruit #3006"]
  SP1 = SPEAKER [package=pcb_mount_speaker]

nets:
  N1: U1.3.3, Part1.VCC, LCD1.pin_1, LCD1.pin_8
  N2: U1.GPIO34, Part1.VERT
  N3: U1.GPIO35, Part1.HORZ
  N4: U1.GPIO33, LCD1.pin4
  N5: U1.GPIO25, Part2.LRCLK
  N6: U1.GPIO26, Part2.BCLK
  N7: U1.GPIO27, LCD1.pin_5
  GND: U1.GPIO11, Part1.GND, Part2.GND
  VIN: U1.VIN, Part2.VIN
  N8: U1.GPIO5, LCD1.pin3
  N9: U1.GPIO18, LCD1.pin_7
  N10: U1.GPIO21, Part2.SD_MODE
  N11: U1.GPIO22, Part2.DIN
  N12: U1.GPIO23, LCD1.pin_6
  N13: U1.GND, LCD1.pin2
  N14: Part2.VO-, SP1.+
  N15: Part2.VO+, SP1.-

custom parts:
  ESP32-38PinWide: Generic 38-Pin ESP32 with wide format (only access to one side of pins on a breadboard) based on Stephen Lilley's HiLetgo ESP-WROOM-32 ESP32 ESP-32S Development Board.
  TFT 1.8 inch 160x128 no SD: This is a generic 1.8 tft spi lcd display available on ebay and others. The 1.8" display has 128x160 color pixels and in this version pin names in breadboard (unlike the real board) and with no SD interface.
  Adafruit MAX98357A I2S 3W Class D Amplifier: Listen to this good news - we now have an all in one digital audio amp breakout board that works incredibly well with the Raspberry Pi! If you're looking for an easy and low cost way to get you digital sound files bumpin' then the MAX08357 I2S Amp Breakout is for you. It takes standard I2S digital audio input and, not only decodes it into analog, but also amplifies it directly into a speaker.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
